# Fritzing sketch Untitled Sketch (saved by Fritzing 0.8.7b)
breadboards: 1

parts:
  U1 = MOC3031-M [package=dil06]
  U2 = MOC3031-M [package=dil06]
  U3 = MOC3031-M [package=dil06]
  R1 = Resistor [tolerance=±5% resistance=220 package=THT]
  Q1 = NPN-Transistor [package="TO92 [THT]"]
  R2 = Resistor [tolerance=±5% resistance=220 package=THT]
  U4 = TRIAC [package=to-92]
  U5 = TRIAC [package=to-92]
  U6 = TRIAC [package=to-92]

nets:
  N1: U1.1, R1.Pin_1
  N2: U1.2, U2.1
  N3: U1.4, U4.G
  N4: U1.6, U4.M1
  N5: U2.2, U3.1
  N6: U2.4, U5.G
  N7: U2.6, U5.M1
  N8: U3.2, Q1.C
  N9: U3.4, U6.G
  N10: U3.6, U6.M1
  N11: Q1.E, R2.Pin_0
  GND: R2.Pin_1
